# Fritzing sketch BlinkwithLED1 (saved by Fritzing 0.9.3b)
breadboards: 1

parts:
  LED_(red) = LED - 5mm [color="Red (633nm)" package="5 mm [THT]"]
  Resistor_(LED) = Resistor [tolerance=±5% resistance=220 package=THT]
  Teensy_3_2 = Teensy 3.2  # not connected

nets:
  N1: LED_(red).anode, Resistor_(LED).Pin_1

notes:
  CST8227 - Interfacing
  Lab 02 - Blink
  Discrete red LED.
  pharasb@AlgonquinCollege.com

custom parts:
  Teensy 3.2: The Teensy is a complete USB-based microcontoller development system, in a very small footprint, capable of implementing many types of projects. All programming is done via the USB port. No special programmer is needed, only a standard micro-USB cable and a PC or Macintosh with a USB port. It has a USB keyboard/mouse/joystick emulation stack and can be programmed through Arduino IDE.
