# Fritzing sketch Lab4 (saved by Fritzing 0.9.4)
breadboards: 1

parts:
  Tri-Colour_LED = RGB LED (com. cathode, rgb) [package="5 mm [THT]"]
  220-Ohm_Resistor_(Green) = Resistor [tolerance=±5% resistance=220 package="2512 [SMD]"]
  220-Ohm_Resistor_(Blue) = Resistor [tolerance=±5% resistance=220 package="2512 [SMD]"]
  220-Ohm_Resistor_(Red) = Resistor [tolerance=±5% resistance=220 package="2512 [SMD]"]
  S1 = Pushbutton [package="[THT]"]
  S2 = Pushbutton [package="[THT]"]
  R1 = Resistor [tolerance=±5% resistance=10k package=THT]
  Teensy_3_1 = Teensy 3.1  # not connected
  R2 = Resistor [tolerance=±5% resistance=10k package=THT]

nets:
  N1: Tri-Colour_LED.red_anode, 220-Ohm_Resistor_(Red).Pin_0
  N2: Tri-Colour_LED.common_cathode, 220-Ohm_Resistor_(Blue).Pin_0
  N3: Tri-Colour_LED.green_anode, S1.Pin_1, S1.Pin_2, S2.Pin_1, S2.Pin_2
  N4: Tri-Colour_LED.blue_anode, 220-Ohm_Resistor_(Green).Pin_0
  N5: S1.Pin_3, S1.Pin_4, R2.Pin_1
  N6: S2.Pin_3, S2.Pin_4, R1.Pin_1
  N7: R1.Pin_0, R2.Pin_0

notes:
  CST8227 – Interfacing
  Lab 04 – Pushbuttons to Control LED Colors
  Control a tri-color RGB with two switches and a pull-up resistor.
  @author Soomin Lee (lee00665)
